# Fritzing sketch due+esp8266 (saved by Fritzing 0.9.3b)

parts:
  Arduino_Due1 = Arduino DUE
  U1 = ESP8266 WiFi Module [part_number=ESP8266]

nets:
  N1: Arduino_Due1.D14, U1.RXD
  N2: Arduino_Due1.D15, U1.TXD
  N3: Arduino_Due1.D53, U1.CH_PD
  N4: Arduino_Due1.GROUND, U1.GND
  3.3V: Arduino_Due1.3.3V, U1.VCC

custom parts:
  Arduino DUE: Arduino Due microcontroller. Breadboard based on photo taken from arduino.cc v1.1
  ESP8266 WiFi Module: Generic WiFi Module based on the ESP8266 with onboard PCB antenna and UART communications
